# Fritzing sketch Lampu4RelayNTP (saved by Fritzing 0.9.3b)

parts:
  U1 = NodeMCU V3.0 CH340G
  U2 = Module 4 Relais 5V [package="Module 4 Relais 5V"]
  BULB1 = Incandescent light bulb small [package="bulb sm"]  # not connected
  BULB2 = Incandescent light bulb small [package="bulb sm"]  # not connected
  BULB3 = Incandescent light bulb small [package="bulb sm"]  # not connected
  BULB4 = Incandescent light bulb small [package="bulb sm"]  # not connected
  Grove1 = Grove OLED 128x96

nets:
  N1: U1.D1, U2.IN1
  N2: U1.D2, Grove1.SCL
  N3: U1.D3, Grove1.SDA
  N4: U1.D4, U2.IN4
  N5: U1.D5, U2.IN2
  N6: U1.D6, U2.IN3
  3V3: U1.3V3, Grove1.VCC
  N7: U1.GND#33, Grove1.GND
  N8: U1.VU, U2.VCC
  N9: U1.GND#41, U2.GND

custom parts:
  NodeMCU V3.0 CH340G: NodeMcu V3 Lua WIFI Development Board
  Module 4 Relais 5V: Module 4 Relais 5V 4x SPD-06VDC-SD-C
